// Logisim project 4bit ALU.circ as structural Verilog
module AND (
  input  [3:0] A,
  input  [3:0] B,
  output [3:0] out_3
);

  assign out_3 = A & B;  // AND_Gate and_1, 4 bits wide
endmodule

module OR (
  input  [3:0] A,
  input  [3:0] B,
  output [3:0] out_3
);

  assign out_3 = A | B;  // OR_Gate or_1, 4 bits wide
endmodule

module XOR (
  input  [3:0] A,
  input  [3:0] B,
  output [3:0] out_3
);

  assign out_3 = A ^ B;  // XOR_Gate xor_1, 4 bits wide
endmodule

module ADD (
  input  in_1,
  input  [3:0] A,
  input  [3:0] B,
  output [3:0] out_4,
  output out_5
);

  Adder #(.width(4)) adder_1 (.a(A), .b(B), .out(out_4), .cin(in_1), .cout(out_5));
endmodule

module ALU (
  input  Cin,
  input  [3:0] INPUT1,
  input  [1:0] in_3,
  input  [3:0] INPUT2,
  output [3:0] OUTPUT,
  output Cout
);

  wire [3:0] add_1_out_4, and_1_out, or_1_out, xor_1_out;

  assign and_1_out = INPUT1 & INPUT2;  // AND_Gate and_1, 4 bits wide
  assign or_1_out = INPUT1 | INPUT2;  // OR_Gate or_1, 4 bits wide
  assign xor_1_out = INPUT1 ^ INPUT2;  // XOR_Gate xor_1, 4 bits wide
  ADD add_1 (.in_1(Cin), .A(INPUT1), .B(INPUT2), .out_4(add_1_out_4), .out_5(Cout));
  Multiplexer #(.select(2), .width(4)) multiplexer_1 (
    .in0(and_1_out), .in1(or_1_out), .in2(xor_1_out), .in3(add_1_out_4), .out(OUTPUT), .sel(in_3));  // open: en
endmodule
