// Logisim project 4bit File Register.circ as structural Verilog: 3 circuits, main circuit ALU&RegisterFile
module ALU (
  input  eN,
  input  Cin,
  input  [15:0] INPUT1,
  input  [1:0] select,
  input  [15:0] INPUT2,
  output [15:0] OUTPUT,
  output Cout
);

  wire [15:0] adder_1_out, and_1_out, or_1_out, xor_1_out;

  assign and_1_out = INPUT1 & INPUT2;  // AND_Gate and_1, 16 bits wide
  assign or_1_out = INPUT1 | INPUT2;  // OR_Gate or_1, 16 bits wide
  assign xor_1_out = INPUT1 ^ INPUT2;  // XOR_Gate xor_1, 16 bits wide
  Adder #(.width(16)) adder_1 (.a(INPUT2), .b(INPUT1), .out(adder_1_out), .cin(Cin), .cout(Cout));
  Multiplexer #(.select(2), .width(16)) multiplexer_1 (
    .in0(and_1_out), .in1(or_1_out), .in2(xor_1_out), .in3(adder_1_out), .out(OUTPUT), .sel(select), .en(eN));
endmodule

module ALU_RegisterFile (
  input  Write_En,
  input  [1:0] Select_Register,
  input  [15:0] Input,
  input  Cin,
  input  En,
  input  select,
  input  [1:0] Read_R1,
  input  [1:0] Read_R2,
  input  [1:0] select_Op,
  input  En_2,
  input  in_11,
  input  in_12,
  output [15:0] ALU_Output,
  output Cout
);

  wire clock_1_out;
  wire [15:0] multiplexer_1_out, register_file_1_data_out_r1, register_file_1_data_out_r2;

  Multiplexer #(.width(16)) multiplexer_1 (
    .in0(Input), .in1(ALU_Output), .out(multiplexer_1_out), .sel(select), .en(En));
  Clock clock_1 (.out(clock_1_out));
  register_file register_file_1 (
    .Write_Enable(Write_En), .R_Select(Select_Register), .Write_Data(multiplexer_1_out), .clk(clock_1_out),
    .read_R1(Read_R1), .read_R2(Read_R2), .in_7(in_11), .in_8(in_12),
    .Data_Out_R2(register_file_1_data_out_r2), .Data_Out_R1(register_file_1_data_out_r1));
  ALU alu_1 (
    .Cin(Cin), .INPUT1(register_file_1_data_out_r1), .select(select_Op),
    .INPUT2(register_file_1_data_out_r2), .OUTPUT(ALU_Output), .eN(En_2), .Cout(Cout));
endmodule

module register_file (
  input  Write_Enable,
  input  [1:0] R_Select,
  input  [15:0] Write_Data,
  input  clk,
  input  [1:0] read_R1,
  input  [1:0] read_R2,
  input  in_7,
  input  in_8,
  output [15:0] Data_Out_R2,
  output [15:0] Data_Out_R1
);

  wire decoder_1_out0, decoder_1_out1, decoder_1_out2, decoder_1_out3;
  wire [15:0] register_1_q, register_2_q, register_3_q, register_4_q;

  Decoder #(.select(2)) decoder_1 (
    .out0(decoder_1_out0), .out1(decoder_1_out1), .out2(decoder_1_out2), .out3(decoder_1_out3),
    .sel(R_Select), .en(Write_Enable));
  Register #(.width(16)) register_1 (.D(Write_Data), .en(decoder_1_out0), .Q(register_1_q), .clk(clk));  // open: clr
  Multiplexer #(.select(2), .width(16)) multiplexer_1 (
    .in0(register_1_q), .in1(register_2_q), .in2(register_3_q), .in3(register_4_q), .out(Data_Out_R1),
    .sel(read_R1), .en(in_8));
  Register #(.width(16)) register_2 (.D(Write_Data), .en(decoder_1_out1), .Q(register_2_q), .clk(clk));  // open: clr
  Multiplexer #(.select(2), .width(16)) multiplexer_2 (
    .in0(register_1_q), .in1(register_2_q), .in2(register_3_q), .in3(register_4_q), .out(Data_Out_R2),
    .sel(read_R2), .en(in_7));
  Register #(.width(16)) register_3 (.D(Write_Data), .en(decoder_1_out2), .Q(register_3_q), .clk(clk));  // open: clr
  Register #(.width(16)) register_4 (.D(Write_Data), .en(decoder_1_out3), .Q(register_4_q), .clk(clk));  // open: clr
endmodule
