// Logisim project ALU32bit.circ as structural Verilog
module alu (
  input  B_inv,
  input  [2:0] op,
  input  Ainv,
  input  [31:0] a,
  input  [31:0] b,
  output Zero,
  output out_7
);

  wire main_1_cout, main_1_result, main_2_cout, main_2_result, main_3_cout, main_3_result, main_4_cout,
       main_4_result, main_5_cout, main_5_result, main_6_cout, main_6_result, main_7_cout, main_7_result,
       main_8_cout, main_8_result, main_9_cout, main_9_result, main_10_cout, main_10_result, main_11_cout,
       main_11_result, main_12_cout, main_12_result, main_13_cout, main_13_result, main_14_cout,
       main_14_result, main_15_cout, main_15_result, main_16_cout, main_16_result, main_17_cout,
       main_17_result, main_18_cout, main_18_result, main_19_cout, main_19_result, main_20_cout,
       main_20_result, main_21_cout, main_21_result, main_22_cout, main_22_result, main_23_cout,
       main_23_result, main_24_cout, main_24_result, main_25_cout, main_25_result, main_26_cout,
       main_26_result, main_27_cout, main_27_result, main_28_cout, main_28_result, main_29_cout,
       main_29_result, main_30_cout, main_30_result, main_31_cout, main_31_result, main_32_result,
       main_32_set;

  main main_1 (
    .a(a[0]), .b(b[0]), .less(main_32_set), .A_inv(Ainv), .B_inv(B_inv), .cin(B_inv), .operation(op),
    .Result(main_1_result), .cout(main_1_cout));  // open: set
  main main_2 (
    .a(a[1]), .b(b[1]), .less(1'b0), .A_inv(Ainv), .B_inv(B_inv), .cin(main_1_cout), .operation(op),
    .Result(main_2_result), .cout(main_2_cout));  // open: set
  main main_3 (
    .a(a[2]), .b(b[2]), .less(1'b0), .A_inv(Ainv), .B_inv(B_inv), .cin(main_2_cout), .operation(op),
    .Result(main_3_result), .cout(main_3_cout));  // open: set
  main main_4 (
    .a(a[3]), .b(b[3]), .less(1'b0), .A_inv(Ainv), .B_inv(B_inv), .cin(main_3_cout), .operation(op),
    .Result(main_4_result), .cout(main_4_cout));  // open: set
  main main_5 (
    .a(a[4]), .b(b[4]), .less(1'b0), .A_inv(Ainv), .B_inv(B_inv), .cin(main_4_cout), .operation(op),
    .Result(main_5_result), .cout(main_5_cout));  // open: set
  main main_6 (
    .a(a[5]), .b(b[5]), .less(1'b0), .A_inv(Ainv), .B_inv(B_inv), .cin(main_5_cout), .operation(op),
    .Result(main_6_result), .cout(main_6_cout));  // open: set
  main main_7 (
    .a(a[6]), .b(b[6]), .less(1'b0), .A_inv(Ainv), .B_inv(B_inv), .cin(main_6_cout), .operation(op),
    .Result(main_7_result), .cout(main_7_cout));  // open: set
  main main_8 (
    .a(a[7]), .b(b[7]), .less(1'b0), .A_inv(Ainv), .B_inv(B_inv), .cin(main_7_cout), .operation(op),
    .Result(main_8_result), .cout(main_8_cout));  // open: set
  main main_9 (
    .a(a[8]), .b(b[8]), .less(1'b0), .A_inv(Ainv), .B_inv(B_inv), .cin(main_8_cout), .operation(op),
    .Result(main_9_result), .cout(main_9_cout));  // open: set
  main main_10 (
    .a(a[9]), .b(b[9]), .less(1'b0), .A_inv(Ainv), .B_inv(B_inv), .cin(main_9_cout), .operation(op),
    .Result(main_10_result), .cout(main_10_cout));  // open: set
  main main_11 (
    .a(a[10]), .b(b[10]), .less(1'b0), .A_inv(Ainv), .B_inv(B_inv), .cin(main_10_cout), .operation(op),
    .Result(main_11_result), .cout(main_11_cout));  // open: set
  main main_12 (
    .a(a[11]), .b(b[11]), .less(1'b0), .A_inv(Ainv), .B_inv(B_inv), .cin(main_11_cout), .operation(op),
    .Result(main_12_result), .cout(main_12_cout));  // open: set
  main main_13 (
    .a(a[12]), .b(b[12]), .less(1'b0), .A_inv(B_inv), .B_inv(B_inv), .cin(main_12_cout), .operation(op),
    .Result(main_13_result), .cout(main_13_cout));  // open: set
  main main_14 (
    .a(a[13]), .b(b[13]), .less(1'b0), .A_inv(Ainv), .B_inv(B_inv), .cin(main_13_cout), .operation(op),
    .Result(main_14_result), .cout(main_14_cout));  // open: set
  main main_15 (
    .a(a[14]), .b(b[14]), .less(1'b0), .A_inv(Ainv), .B_inv(B_inv), .cin(main_14_cout), .operation(op),
    .Result(main_15_result), .cout(main_15_cout));  // open: set
  main main_16 (
    .a(a[15]), .b(b[15]), .less(1'b0), .A_inv(Ainv), .B_inv(B_inv), .cin(main_15_cout), .operation(op),
    .Result(main_16_result), .cout(main_16_cout));  // open: set
  main main_17 (
    .a(a[16]), .b(b[16]), .less(1'b0), .A_inv(Ainv), .B_inv(B_inv), .cin(main_16_cout), .operation(op),
    .Result(main_17_result), .cout(main_17_cout));  // open: set
  main main_18 (
    .a(a[17]), .b(b[17]), .less(1'b0), .A_inv(Ainv), .B_inv(B_inv), .cin(main_17_cout), .operation(op),
    .Result(main_18_result), .cout(main_18_cout));  // open: set
  main main_19 (
    .a(a[18]), .b(b[18]), .less(1'b0), .A_inv(Ainv), .B_inv(B_inv), .cin(main_18_cout), .operation(op),
    .Result(main_19_result), .cout(main_19_cout));  // open: set
  main main_20 (
    .a(a[19]), .b(b[19]), .less(1'b0), .A_inv(Ainv), .B_inv(B_inv), .cin(main_19_cout), .operation(op),
    .Result(main_20_result), .cout(main_20_cout));  // open: set
  main main_21 (
    .a(a[20]), .b(b[20]), .less(1'b0), .A_inv(Ainv), .B_inv(B_inv), .cin(main_20_cout), .operation(op),
    .Result(main_21_result), .cout(main_21_cout));  // open: set
  main main_22 (
    .a(a[21]), .b(b[21]), .less(1'b0), .A_inv(Ainv), .B_inv(B_inv), .cin(main_21_cout), .operation(op),
    .Result(main_22_result), .cout(main_22_cout));  // open: set
  main main_23 (
    .a(a[22]), .b(b[22]), .less(1'b0), .A_inv(Ainv), .B_inv(B_inv), .cin(main_22_cout), .operation(op),
    .Result(main_23_result), .cout(main_23_cout));  // open: set
  main main_24 (
    .a(a[23]), .b(b[23]), .less(1'b0), .A_inv(Ainv), .B_inv(B_inv), .cin(main_23_cout), .operation(op),
    .Result(main_24_result), .cout(main_24_cout));  // open: set
  main main_25 (
    .a(a[24]), .b(b[24]), .less(1'b0), .A_inv(Ainv), .B_inv(B_inv), .cin(main_24_cout), .operation(op),
    .Result(main_25_result), .cout(main_25_cout));  // open: set
  main main_26 (
    .a(a[25]), .b(b[25]), .less(1'b0), .A_inv(Ainv), .B_inv(B_inv), .cin(main_25_cout), .operation(op),
    .Result(main_26_result), .cout(main_26_cout));  // open: set
  main main_27 (
    .a(a[26]), .b(b[26]), .less(1'b0), .A_inv(Ainv), .B_inv(B_inv), .cin(main_26_cout), .operation(op),
    .Result(main_27_result), .cout(main_27_cout));  // open: set
  main main_28 (
    .a(a[27]), .b(b[27]), .less(1'b0), .A_inv(Ainv), .B_inv(B_inv), .cin(main_27_cout), .operation(op),
    .Result(main_28_result), .cout(main_28_cout));  // open: set
  main main_29 (
    .a(a[28]), .b(b[28]), .less(1'b0), .A_inv(Ainv), .B_inv(B_inv), .cin(main_28_cout), .operation(op),
    .Result(main_29_result), .cout(main_29_cout));  // open: set
  main main_30 (
    .a(a[29]), .b(b[29]), .less(1'b0), .A_inv(Ainv), .B_inv(B_inv), .cin(main_29_cout), .operation(op),
    .Result(main_30_result), .cout(main_30_cout));  // open: set
  main main_31 (
    .a(a[30]), .b(b[30]), .less(1'b0), .A_inv(Ainv), .B_inv(B_inv), .cin(main_30_cout), .operation(op),
    .Result(main_31_result), .cout(main_31_cout));  // open: set
  main main_32 (
    .a(a[31]), .b(b[31]), .less(1'b0), .A_inv(Ainv), .B_inv(B_inv), .cin(main_31_cout), .operation(op),
    .Result(main_32_result), .set(main_32_set), .cout(out_7));
  nor nor_1 (Zero, main_1_result, main_2_result, main_3_result, main_4_result, main_5_result, main_6_result, main_7_result, main_8_result, main_9_result, main_10_result, main_11_result, main_12_result, main_13_result, main_14_result, main_15_result, main_16_result, main_17_result, main_18_result, main_19_result, main_20_result, main_21_result, main_22_result, main_23_result, main_24_result, main_25_result, main_26_result, main_27_result, main_28_result, main_29_result, main_30_result, main_31_result, main_32_result);
endmodule

module main (
  input  A_inv,
  input  B_inv,
  input  cin,
  input  [2:0] operation,
  input  a,
  input  b,
  input  less,
  output Result,
  output set,
  output cout
);

  wire and_1_out, multiplexer_1_out, multiplexer_2_out, nor_1_out, not_1_out, not_2_out, or_1_out, xor_1_out;

  Multiplexer multiplexer_1 (.in0(a), .in1(not_1_out), .out(multiplexer_1_out), .sel(A_inv));  // open: en
  not not_1 (not_1_out, a);
  Multiplexer multiplexer_2 (.in0(b), .in1(not_2_out), .out(multiplexer_2_out), .sel(B_inv));  // open: en
  not not_2 (not_2_out, b);
  and and_1 (and_1_out, multiplexer_1_out, multiplexer_2_out);
  or or_1 (or_1_out, multiplexer_1_out, multiplexer_2_out);
  xor xor_1 (xor_1_out, multiplexer_1_out, multiplexer_2_out);
  nor nor_1 (nor_1_out, multiplexer_1_out, multiplexer_2_out);
  Adder #(.width(1)) adder_1 (.a(multiplexer_1_out), .b(multiplexer_2_out), .out(set), .cin(cin), .cout(cout));
  Multiplexer #(.select(3)) multiplexer_3 (
    .in0(and_1_out), .in1(or_1_out), .in2(xor_1_out), .in3(nor_1_out), .in4(set), .in5(less), .out(Result),
    .sel(operation));  // open: in6, in7, en
endmodule
