// Logisim project CPU.circ as structural Verilog: 17 circuits, main circuit main
module main (
  input  clear,
  input  clr,
  output [31:0] Read_Data_1
);

  wire alu_control_1_a_inverse, alu_control_1_b_inverse, alu_control_1_jr, alu_control_1_shift16bit, beq_out,
       bne_out, clock_1_out, control_1_aluop0, control_1_aluop1, control_1_aluop2, control_1_aluop3,
       control_1_alusrc, control_1_beq_bne, control_1_branch, control_1_jump, control_1_memread,
       control_1_memwrite, control_1_regwrite, multiplexer_8_out, n32bit_alu_1_zero_signal;
  wire [1:0] control_1_extop, control_1_memtoreg, control_1_regdst;
  wire [2:0] alu_control_1_s0;
  wire [4:0] multiplexer_4_out, multiplexer_7_out, splitter_1_dist, splitter_1_shamt, splitter_1_src_1,
       splitter_1_src_2;
  wire [5:0] splitter_1_funct, splitter_1_opcode;
  wire [15:0] splitter_1_immdea;
  wire [23:0] mem_splt_1_out_2, mem_splt_2_out_2;
  wire [25:0] splitter_1_jump;
  wire [27:0] shiftlift2bit_1__28bit_output;
  wire [31:0] adder_1_out, adder_2_out, multiplexer_1_out, multiplexer_2_out, multiplexer_3_out,
       multiplexer_5_out, multiplexer_6_out, multiplexer_9_out, o_extend_1__32bit_output, ram_1_data,
       register_1_q, registerfile_1_1_read_data_1, registerfile_1_1_read_data_2, rom_1_data,
       s_extend_1__32bit_output, shift_32bit_1__32bit_output, split28to32_1__32bit_output,
       z_extend_1__32bit_output;

  Adder #(.width(32)) adder_1 (.a(register_1_q), .b(32'h4), .out(adder_1_out));  // open: cin, cout
  Clock clock_1 (.out(clock_1_out));
  Register #(.width(32)) register_1 (
    .D(multiplexer_2_out), .Q(register_1_q), .clk(clock_1_out), .clr(clear));  // open: en
  mem_splt mem_splt_1 (.in_1(register_1_q), .out_2(mem_splt_1_out_2));
  shift_32bit shift_32bit_1 (._32bit_input(multiplexer_5_out), ._32bit_output(shift_32bit_1__32bit_output));
  control control_1 (
    .OP0(splitter_1_opcode[0]), .OP1(splitter_1_opcode[1]), .OP2(splitter_1_opcode[2]),
    .OP3(splitter_1_opcode[3]), .OP4(splitter_1_opcode[4]), .OP5(splitter_1_opcode[5]),
    .RegDst(control_1_regdst), .ALUSrc(control_1_alusrc), .MemtoReg(control_1_memtoreg),
    .MemRead(control_1_memread), .MemWrite(control_1_memwrite), .ExtOp(control_1_extop),
    .Branch(control_1_branch), .Jump(control_1_jump), .ALUOp0(control_1_aluop0), .ALUOp1(control_1_aluop1),
    .ALUOp2(control_1_aluop2), .ALUOp3(control_1_aluop3), .RegWrite(control_1_regwrite),
    .beq_bne(control_1_beq_bne));
  Adder #(.width(32)) adder_2 (.a(shift_32bit_1__32bit_output), .b(adder_1_out), .out(adder_2_out));  // open: cin, cout
  ROM #(.addrWidth(24), .dataWidth(32)) rom_1 (.addr(mem_splt_1_out_2), .data(rom_1_data));  // open: sel
  ShiftLift2bit shiftlift2bit_1 (._26bit_input(splitter_1_jump), ._28bit_output(shiftlift2bit_1__28bit_output));
  Multiplexer #(.width(32)) multiplexer_1 (
    .in0(adder_1_out), .in1(adder_2_out), .out(multiplexer_1_out), .sel(multiplexer_8_out));  // open: en
  Splitter splitter_1 (
    .in_1(rom_1_data), .funct(splitter_1_funct), .shamt(splitter_1_shamt), .\dist (splitter_1_dist),
    .src_2(splitter_1_src_2), .src_1(splitter_1_src_1), .OPCode(splitter_1_opcode),
    .immdea(splitter_1_immdea), .jump(splitter_1_jump));
  split28to32 split28to32_1 (
    ._28bit_input(shiftlift2bit_1__28bit_output), .last4bitInPC(splitter_1_opcode[5:2]),
    ._32bit_output(split28to32_1__32bit_output));
  S_Extend s_extend_1 (._16bit_input(splitter_1_immdea), ._32bit_output(s_extend_1__32bit_output));
  Z_Extend z_extend_1 (._16bit_input(splitter_1_immdea), ._32bit_output(z_extend_1__32bit_output));
  O_Extend o_extend_1 (._16bit_input(splitter_1_immdea), ._32bit_output(o_extend_1__32bit_output));
  Multiplexer #(.width(32)) multiplexer_2 (
    .in0(multiplexer_3_out), .in1(registerfile_1_1_read_data_1), .out(multiplexer_2_out),
    .sel(alu_control_1_jr));  // open: en
  Multiplexer #(.width(32)) multiplexer_3 (
    .in0(multiplexer_1_out), .in1(split28to32_1__32bit_output), .out(multiplexer_3_out), .sel(control_1_jump));  // open: en
  Multiplexer #(.select(2), .width(5)) multiplexer_4 (
    .in0(splitter_1_dist), .in1(splitter_1_src_2), .in2({5{1'b1}}), .out(multiplexer_4_out),
    .sel(control_1_regdst));  // open: in3, en
  Multiplexer #(.select(2), .width(32)) multiplexer_5 (
    .in0(s_extend_1__32bit_output), .in1(z_extend_1__32bit_output), .in2(o_extend_1__32bit_output),
    .out(multiplexer_5_out), .sel(control_1_extop));  // open: in3, en
  RegisterFile_1 registerfile_1_1 (
    .Write_Data(multiplexer_9_out), .\dist (multiplexer_4_out), .src_1(splitter_1_src_1),
    .src_2(splitter_1_src_2), .clk(clock_1_out), .RegWrite(control_1_regwrite),
    .Read_Data_1(registerfile_1_1_read_data_1), .Read_Data_2(registerfile_1_1_read_data_2));
  Multiplexer #(.width(32)) multiplexer_6 (
    .in0(registerfile_1_1_read_data_2), .in1(multiplexer_5_out), .out(multiplexer_6_out),
    .sel(control_1_alusrc));  // open: en
  _32bit_ALU u_32bit_alu_1 (
    .INPUT1(registerfile_1_1_read_data_1), .Ainv(alu_control_1_a_inverse), .SA(multiplexer_7_out),
    .Binv(alu_control_1_b_inverse), .select(alu_control_1_s0), .INPUT2(multiplexer_6_out),
    .OUTPUT(Read_Data_1), .zero_signal(n32bit_alu_1_zero_signal));  // open: Cout
  ALU_Control alu_control_1 (
    .ALU_op0(control_1_aluop0), .ALU_op1(control_1_aluop1), .ALU_op2(control_1_aluop2),
    .ALU_op3(control_1_aluop3), .f0(splitter_1_funct[0]), .f1(splitter_1_funct[1]), .f2(splitter_1_funct[2]),
    .f3(splitter_1_funct[3]), .f4(splitter_1_funct[4]), .f5(splitter_1_funct[5]), .s0(alu_control_1_s0[0]),
    .S1(alu_control_1_s0[1]), .S2(alu_control_1_s0[2]), .B_inverse(alu_control_1_b_inverse),
    .A_inverse(alu_control_1_a_inverse), .shift16bit(alu_control_1_shift16bit), .jr(alu_control_1_jr));
  mem_splt mem_splt_2 (.in_1(Read_Data_1), .out_2(mem_splt_2_out_2));
  and bne (bne_out, ~n32bit_alu_1_zero_signal, control_1_branch);  // AND_Gate
  and beq (beq_out, n32bit_alu_1_zero_signal, control_1_branch);
  Multiplexer #(.width(5)) multiplexer_7 (
    .in0(splitter_1_shamt), .in1(5'b10000), .out(multiplexer_7_out), .sel(alu_control_1_shift16bit));  // open: en
  RAM #(.addrWidth(24), .dataWidth(32), .bus("separate")) ram_1 (
    .addr(mem_splt_2_out_2), .din(registerfile_1_1_read_data_2), .data(ram_1_data), .str(control_1_memwrite),
    .clk(clock_1_out), .ld(control_1_memread), .clr(clr));  // open: sel
  Multiplexer multiplexer_8 (
    .in0(bne_out), .in1(beq_out), .out(multiplexer_8_out), .sel(control_1_beq_bne));  // open: en
  Multiplexer #(.select(2), .width(32)) multiplexer_9 (
    .in0(ram_1_data), .in1(Read_Data_1), .in2(adder_1_out), .out(multiplexer_9_out), .sel(control_1_memtoreg));  // open: in3, en

  // Notes on the sheet:
  //   contents of rom_1 (hex, n*v repeats v):
  //   4*0 a4880
endmodule

module _1bit_ALU (
  input  A_inv,
  input  B_inv,
  input  cin,
  input  [2:0] operation,
  input  a,
  input  b,
  input  less,
  output Result,
  output set,
  output cout
);

  wire and_1_out, multiplexer_1_out, multiplexer_2_out, nor_1_out, not_1_out, not_2_out, or_1_out, xor_1_out;

  Multiplexer multiplexer_1 (.in0(a), .in1(not_1_out), .out(multiplexer_1_out), .sel(A_inv));  // open: en
  not not_1 (not_1_out, a);
  Multiplexer multiplexer_2 (.in0(b), .in1(not_2_out), .out(multiplexer_2_out), .sel(B_inv));  // open: en
  not not_2 (not_2_out, b);
  and and_1 (and_1_out, multiplexer_1_out, multiplexer_2_out);
  or or_1 (or_1_out, multiplexer_1_out, multiplexer_2_out);
  xor xor_1 (xor_1_out, multiplexer_1_out, multiplexer_2_out);
  nor nor_1 (nor_1_out, multiplexer_1_out, multiplexer_2_out);
  Adder #(.width(1)) adder_1 (.a(multiplexer_1_out), .b(multiplexer_2_out), .out(set), .cin(cin), .cout(cout));
  Multiplexer #(.select(3)) multiplexer_3 (
    .in0(and_1_out), .in1(or_1_out), .in2(xor_1_out), .in3(nor_1_out), .in4(set), .in5(less), .out(Result),
    .sel(operation));  // open: in6, in7, en
endmodule

module ALU_RegisterFile (
  input  Write_En,
  input  [1:0] Select_Register,
  input  [3:0] Input,
  input  Cin,
  input  En,
  input  select,
  input  [1:0] Read_R1,
  input  [1:0] Read_R2,
  input  [1:0] select_Op,
  input  En_2,
  input  in_11,
  input  in_12,
  output [3:0] ALU_Output,
  output Cout
);

  wire clock_1_out;
  wire [3:0] multiplexer_1_out, register_file_1_data_out_r1, register_file_1_data_out_r2;

  Multiplexer #(.width(4)) multiplexer_1 (
    .in0(Input), .in1(ALU_Output), .out(multiplexer_1_out), .sel(select), .en(En));
  Clock clock_1 (.out(clock_1_out));
  register_file register_file_1 (
    .Write_Enable(Write_En), .R_Select(Select_Register), .Write_Data(multiplexer_1_out), .clk(clock_1_out),
    .read_R1(Read_R1), .read_R2(Read_R2), .in_7(in_11), .in_8(in_12),
    .Data_Out_R2(register_file_1_data_out_r2), .Data_Out_R1(register_file_1_data_out_r1));
  // _1bit_ALU 1bit_alu_1: pin names not known; wires that end beside it: register_file_1_data_out_r1, select_Op, Cin, register_file_1_data_out_r2, ALU_Output, En_2, Cout
endmodule

module register_file (
  input  Write_Enable,
  input  [1:0] R_Select,
  input  [3:0] Write_Data,
  input  clk,
  input  [1:0] read_R1,
  input  [1:0] read_R2,
  input  in_7,
  input  in_8,
  output [3:0] Data_Out_R2,
  output [3:0] Data_Out_R1
);

  wire decoder_1_out0, decoder_1_out1, decoder_1_out2, decoder_1_out3;
  wire [3:0] register_1_q, register_2_q, register_3_q, register_4_q;

  Decoder #(.select(2)) decoder_1 (
    .out0(decoder_1_out0), .out1(decoder_1_out1), .out2(decoder_1_out2), .out3(decoder_1_out3),
    .sel(R_Select), .en(Write_Enable));
  Register #(.width(4)) register_1 (.D(Write_Data), .en(decoder_1_out0), .Q(register_1_q), .clk(clk));  // open: clr
  Multiplexer #(.select(2), .width(4)) multiplexer_1 (
    .in0(register_1_q), .in1(register_2_q), .in2(register_3_q), .in3(register_4_q), .out(Data_Out_R1),
    .sel(read_R1), .en(in_8));
  Register #(.width(4)) register_2 (.D(Write_Data), .en(decoder_1_out1), .Q(register_2_q), .clk(clk));  // open: clr
  Multiplexer #(.select(2), .width(4)) multiplexer_2 (
    .in0(register_1_q), .in1(register_2_q), .in2(register_3_q), .in3(register_4_q), .out(Data_Out_R2),
    .sel(read_R2), .en(in_7));
  Register #(.width(4)) register_3 (.D(Write_Data), .en(decoder_1_out2), .Q(register_3_q), .clk(clk));  // open: clr
  Register #(.width(4)) register_4 (.D(Write_Data), .en(decoder_1_out3), .Q(register_4_q), .clk(clk));  // open: clr
endmodule

// S-Ex
module S_Extend (
  input  [15:0] _16bit_input,
  output [31:0] _32bit_output
);


  assign _32bit_output = {{17{_16bit_input[15]}}, _16bit_input[14:0]};
endmodule

// Z-Ex
module Z_Extend (
  input  [15:0] _16bit_input,
  output [31:0] _32bit_output
);


  assign _32bit_output = {{16{1'b0}}, _16bit_input};
endmodule

// O-Ex
module O_Extend (
  input  [15:0] _16bit_input,
  output [31:0] _32bit_output
);


  assign _32bit_output = {{16{1'b1}}, _16bit_input};
endmodule

module RegisterFile_1 (
  input  [31:0] Write_Data,
  input  clk,
  input  RegWrite,
  input  [4:0] \dist ,
  input  [4:0] src_1,
  input  [4:0] src_2,
  output [31:0] Read_Data_1,
  output [31:0] Read_Data_2
);

  // RegisterFile registerfile_1: pin names not known; wires that end beside it: Write_Data, clk, RegWrite, \dist , src_1, src_2, Read_Data_1, Read_Data_2
endmodule

module Splitter (
  input  [31:0] in_1,
  output [5:0] funct,
  output [4:0] shamt,
  output [4:0] \dist ,
  output [4:0] src_2,
  output [4:0] src_1,
  output [5:0] OPCode,
  output [15:0] immdea,
  output [25:0] jump
);


  assign \dist  = in_1[15:11];
  assign funct = in_1[5:0];
  assign immdea = in_1[15:0];
  assign jump = in_1[25:0];
  assign OPCode = in_1[31:26];
  assign shamt = in_1[10:6];
  assign src_1 = in_1[25:21];
  assign src_2 = in_1[20:16];
endmodule

// Lui-Ex
module luiEx (
  input  [15:0] _16bit_input,
  output [31:0] _32bit_output
);


  assign _32bit_output = {_16bit_input, {16{1'b0}}};
endmodule

module ShiftLift2bit (
  input  [25:0] _26bit_input,
  output [27:0] _28bit_output
);


  assign _28bit_output = {_26bit_input, 2'b00};
endmodule

module _32bit_ALU (
  input  [31:0] INPUT1,
  input  Ainv,
  input  [4:0] SA,
  input  Binv,
  input  [2:0] select,
  input  [31:0] INPUT2,
  output [31:0] OUTPUT,
  output Cout,
  output zero_signal
);

  wire [31:0] adder_1_out, and_1_out, multiplexer_1_out, multiplexer_2_out, not_1_out, not_2_out, or_1_out,
       shifter_1_out, xor_1_out;

  Multiplexer #(.width(32)) multiplexer_1 (
    .in0(INPUT1), .in1(not_1_out), .out(multiplexer_1_out), .sel(Ainv));  // open: en
  assign not_1_out = ~INPUT1;  // NOT_Gate not_1, 32 bits wide
  assign not_2_out = ~INPUT2;  // NOT_Gate not_2, 32 bits wide
  Multiplexer #(.width(32)) multiplexer_2 (
    .in0(INPUT2), .in1(not_2_out), .out(multiplexer_2_out), .sel(Binv));  // open: en
  assign and_1_out = multiplexer_1_out & multiplexer_2_out;  // AND_Gate and_1, 32 bits wide
  assign or_1_out = multiplexer_1_out | multiplexer_2_out;  // OR_Gate or_1, 32 bits wide
  assign xor_1_out = multiplexer_1_out ^ multiplexer_2_out;  // XOR_Gate xor_1, 32 bits wide
  Adder #(.width(32)) adder_1 (
    .a(multiplexer_1_out), .b(multiplexer_2_out), .out(adder_1_out), .cin(Binv), .cout(Cout));
  Shifter #(.width(32)) shifter_1 (.in(multiplexer_2_out), .\dist (SA), .out(shifter_1_out));
  Multiplexer #(.select(3), .width(32)) multiplexer_3 (
    .in0(and_1_out), .in1(or_1_out), .in2(xor_1_out), .in3(adder_1_out), .in4({{31{1'b0}}, adder_1_out[31]}),
    .in5(shifter_1_out), .out(OUTPUT), .sel(select));  // open: in6, in7, en
  nor nor_1 (zero_signal, OUTPUT[0], OUTPUT[1], OUTPUT[2], OUTPUT[3], OUTPUT[4], OUTPUT[5], OUTPUT[6], OUTPUT[7], OUTPUT[8], OUTPUT[9], OUTPUT[10], OUTPUT[11], OUTPUT[12], OUTPUT[13], OUTPUT[14], OUTPUT[15], OUTPUT[16], OUTPUT[17], OUTPUT[18], OUTPUT[19], OUTPUT[20], OUTPUT[21], OUTPUT[22], OUTPUT[23], OUTPUT[24], OUTPUT[25], OUTPUT[26], OUTPUT[27], OUTPUT[28], OUTPUT[29], OUTPUT[30], OUTPUT[31]);
endmodule

// shift2bit
module shift_32bit (
  input  [31:0] _32bit_input,
  output [31:0] _32bit_output
);

  Shifter #(.width(32)) shifter_1 (.in(_32bit_input), .\dist (5'b00010), .out(_32bit_output));
endmodule

module control (
  input  OP0,
  input  OP1,
  input  OP2,
  input  OP3,
  input  OP4,
  input  OP5,
  output [1:0] RegDst,
  output ALUSrc,
  output [1:0] MemtoReg,
  output MemRead,
  output MemWrite,
  output [1:0] ExtOp,
  output Branch,
  output Jump,
  output ALUOp0,
  output ALUOp1,
  output ALUOp2,
  output ALUOp3,
  output RegWrite,
  output beq_bne
);

  wire Addi_out, bne_out, lui_out, ori_out, r_type_out, Xori_out;
  wire [0:0] or_1_out, or_3_out, Z___Ex_out;
  wire [1:1] Andi_out;

  and beq (beq_bne, ~OP5, ~OP4, ~OP3, OP2, ~OP1, ~OP0);  // AND_Gate
  and Andi (Andi_out[1], ~OP5, ~OP4, OP3, OP2, ~OP1, ~OP0);  // AND_Gate
  and Addi (Addi_out, ~OP5, ~OP4, OP3, ~OP2, ~OP1, ~OP0);  // AND_Gate
  and Xori (Xori_out, ~OP5, ~OP4, OP3, OP2, OP1, ~OP0);  // AND_Gate
  and lui (lui_out, ~OP5, ~OP4, OP3, OP2, OP1, OP0);  // AND_Gate
  and ori (ori_out, ~OP5, ~OP4, OP3, OP2, ~OP1, OP0);  // AND_Gate
  and jal (Jump, ~OP5, ~OP4, ~OP3, ~OP2, OP1, ~OP0);  // AND_Gate
  and bne (bne_out, ~OP5, ~OP4, ~OP3, OP2, ~OP1, OP0);  // AND_Gate
  and sw (MemWrite, OP5, ~OP4, OP3, ~OP2, OP1, OP0);  // AND_Gate
  and lw (MemRead, OP5, ~OP4, ~OP3, ~OP2, OP1, OP0);  // AND_Gate
  and r_type (r_type_out, ~OP5, ~OP4, ~OP3, ~OP2, ~OP1, ~OP0);  // AND_Gate
  or or_1 (or_1_out[0], r_type_out, ori_out, Xori_out, Addi_out, Andi_out[1], lui_out);
  or Z___Ex (Z___Ex_out[0], ori_out, Xori_out);
  or or_2 (Branch, bne_out, beq_bne);
  or or_3 (or_3_out[0], lui_out, MemRead, MemWrite, Andi_out[1], ori_out, Xori_out, Addi_out);
  or or_4 (ALUOp0, bne_out, Andi_out[1], Xori_out, Jump, beq_bne);
  or or_5 (ALUOp1, ori_out, Addi_out, Xori_out, Jump, beq_bne);
  or or_6 (ALUOp2, r_type_out, Andi_out[1], Xori_out, Addi_out, Jump);
  or or_7 (ALUOp3, Xori_out, lui_out);
  or or_8 (RegWrite, r_type_out, MemRead, ori_out, lui_out, Xori_out, Addi_out, Andi_out[1], Jump);
  assign RegDst = {1'b0, or_3_out[0]} | {Jump, 1'b0};  // OR_Gate or_9, 2 bits wide
  assign MemtoReg = {Jump, 1'b0} | {1'b0, or_1_out[0]};  // OR_Gate or_10, 2 bits wide
  assign ExtOp = {1'b0, Z___Ex_out[0]} | {Andi_out[1], 1'b0};  // OR_Gate or_11, 2 bits wide
  or or_12 (ALUSrc, MemWrite, MemRead, Xori_out, lui_out, Addi_out, ori_out, Andi_out[1]);
endmodule

module ALU_Control (
  input  ALU_op0,
  input  ALU_op1,
  input  ALU_op2,
  input  ALU_op3,
  input  f0,
  input  f1,
  input  f2,
  input  f3,
  input  f4,
  input  f5,
  output s0,
  output S1,
  output S2,
  output B_inverse,
  output A_inverse,
  output shift16bit,
  output jr
);

  wire add_out, addi_out, beq_out, bne_out, lw_sw_out, or_out, ori_out, sll_out, slt_out, Sub_out, xor_out,
       xori_out;

  and lw_sw (lw_sw_out, ~ALU_op0, ~ALU_op1, ~ALU_op2, ~ALU_op3);  // AND_Gate
  and bne (bne_out, ALU_op0, ~ALU_op1, ~ALU_op2, ~ALU_op3);  // AND_Gate
  and beq (beq_out, ALU_op0, ALU_op1, ~ALU_op2, ~ALU_op3);  // AND_Gate
  and ori (ori_out, ~ALU_op0, ALU_op1, ~ALU_op2, ~ALU_op3);  // AND_Gate
  // AND_Gate andi has open pins: in0=ALU_op0, in1=ALU_op1, in2=ALU_op2, in3=ALU_op3, out=open
  and addi (addi_out, ~ALU_op0, ALU_op1, ALU_op2, ~ALU_op3);  // AND_Gate
  and xori (xori_out, ALU_op0, ALU_op1, ALU_op2, ALU_op3);
  and lui (shift16bit, ~ALU_op0, ~ALU_op1, ~ALU_op2, ALU_op3);  // AND_Gate
  // AND_Gate jal has open pins: in0=ALU_op0, in1=ALU_op1, in2=ALU_op2, in3=ALU_op3, out=open
  and add (add_out, ~f0, ~f1, ~f2, ~f3, ~f4, f5, ~ALU_op0, ~ALU_op1, ALU_op2, ~ALU_op3);  // AND_Gate
  and \or  (or_out, f0, ~f1, f2, ~f3, ~f4, f5, ~ALU_op0, ~ALU_op1, ALU_op2, ~ALU_op3);  // AND_Gate
  and \xor  (xor_out, ~f0, f1, f2, ~f3, ~f4, f5, ~ALU_op0, ~ALU_op1, ALU_op2, ~ALU_op3);  // AND_Gate
  and \nor  (A_inverse, f0, f1, f2, ~f3, ~f4, f5, ~ALU_op0, ~ALU_op1, ALU_op2, ~ALU_op3);  // AND_Gate
  // AND_Gate and has open pins: in0=f0, in1=f1, in2=f2, in3=f3, in4=f4, in5=f5, in6=ALU_op0, in7=ALU_op1, in8=ALU_op2, in9=ALU_op3, out=open
  and Sub (Sub_out, ~f0, f1, ~f2, ~f3, ~f4, f5, ~ALU_op0, ~ALU_op1, ALU_op2, ~ALU_op3);  // AND_Gate
  and slt (slt_out, ~f0, f1, ~f2, f3, ~f4, f5, ~ALU_op0, ~ALU_op1, ALU_op2, ~ALU_op3);  // AND_Gate
  and u_jr (jr, ~f0, ~f1, ~f2, f3, ~f4, ~f5, ~ALU_op0, ~ALU_op1, ALU_op2, ~ALU_op3);  // AND_Gate
  and sll (sll_out, ~f0, ~f1, ~f2, ~f3, ~f4, ~f5, ~ALU_op0, ~ALU_op1, ALU_op2, ~ALU_op3);  // AND_Gate
  or or_2 (s0, lw_sw_out, bne_out, ori_out, shift16bit, addi_out, add_out, beq_out, sll_out, or_out, Sub_out);
  or or_3 (S1, lw_sw_out, bne_out, addi_out, xori_out, add_out, beq_out, xor_out, Sub_out);
  or or_4 (S2, slt_out, shift16bit, sll_out);
  or or_5 (B_inverse, bne_out, A_inverse, Sub_out, slt_out, beq_out);
endmodule

module split28to32 (
  input  [27:0] _28bit_input,
  input  [3:0] last4bitInPC,
  output [31:0] _32bit_output
);


  assign _32bit_output = {last4bitInPC, _28bit_input};
endmodule

module mem_splt (
  input  [31:0] in_1,
  output [23:0] out_2
);


  assign out_2 = in_1[23:0];
endmodule
