// Logisim project New_ALU (1).circ as structural Verilog: 2 circuits, main circuit Alu Ib
module Alu_Ib (
  input  Binverte,
  input  Ainverte,
  input  carry_in,
  input  [1:0] operation,
  input  a,
  input  b,
  input  slt,
  output result,
  output carry_out,
  output sign
);

  wire and_1_out, multiplexer_1_out, multiplexer_2_out, not_1_out, not_2_out, or_1_out;

  not not_1 (not_1_out, a);
  not not_2 (not_2_out, b);
  Multiplexer #(.disabled(0), .enable("false")) multiplexer_1 (
    .in0(a), .in1(not_1_out), .out(multiplexer_1_out), .sel(Ainverte));
  Multiplexer #(.disabled(0), .enable("false")) multiplexer_2 (
    .in0(b), .in1(not_2_out), .out(multiplexer_2_out), .sel(Binverte));
  and and_1 (and_1_out, multiplexer_1_out, multiplexer_2_out);
  or or_1 (or_1_out, multiplexer_1_out, multiplexer_2_out);
  Adder #(.width(1)) adder_1 (
    .a(multiplexer_1_out), .b(multiplexer_2_out), .out(sign), .cin(carry_in), .cout(carry_out));
  Multiplexer #(.select(2), .enable("false")) multiplexer_3 (
    .in0(and_1_out), .in1(or_1_out), .in2(sign), .in3(slt), .out(result), .sel(operation));
endmodule

module Alu_32bit (
  input  [31:0] in_1,
  input  [31:0] in_2,
  input  in_3,
  input  in_4,
  input  [1:0] in_5,
  output zero,
  output [31:0] out_7
);

  wire alu_ib_1_carry_out, alu_ib_2_carry_out, alu_ib_3_carry_out, alu_ib_4_carry_out, alu_ib_5_carry_out,
       alu_ib_6_carry_out, alu_ib_7_carry_out, alu_ib_8_carry_out, alu_ib_9_carry_out, alu_ib_10_carry_out,
       alu_ib_11_carry_out, alu_ib_12_carry_out, alu_ib_13_carry_out, alu_ib_14_carry_out,
       alu_ib_15_carry_out, alu_ib_16_carry_out, alu_ib_17_carry_out, alu_ib_18_carry_out,
       alu_ib_19_carry_out, alu_ib_20_carry_out, alu_ib_21_carry_out, alu_ib_22_carry_out,
       alu_ib_23_carry_out, alu_ib_24_carry_out, alu_ib_25_carry_out, alu_ib_26_carry_out,
       alu_ib_27_carry_out, alu_ib_28_carry_out, alu_ib_29_carry_out, alu_ib_30_carry_out,
       alu_ib_31_carry_out, alu_ib_32_sign;

  Alu_Ib alu_ib_1 (
    .a(in_2[0]), .b(in_1[0]), .slt(alu_ib_32_sign), .result(out_7[0]), .Binverte(in_3), .Ainverte(in_4),
    .carry_in(in_4), .operation(in_5), .carry_out(alu_ib_1_carry_out));  // open: sign
  Alu_Ib alu_ib_2 (
    .a(in_2[1]), .b(in_1[1]), .slt(1'b0), .result(out_7[1]), .Binverte(in_3), .Ainverte(in_4),
    .carry_in(alu_ib_1_carry_out), .operation(in_5), .carry_out(alu_ib_2_carry_out));  // open: sign
  Alu_Ib alu_ib_3 (
    .a(in_2[2]), .b(in_1[2]), .slt(1'b0), .result(out_7[2]), .Binverte(in_3), .Ainverte(in_4),
    .carry_in(alu_ib_2_carry_out), .operation(in_5), .carry_out(alu_ib_3_carry_out));  // open: sign
  Alu_Ib alu_ib_4 (
    .a(in_2[3]), .b(in_1[3]), .slt(1'b0), .result(out_7[3]), .Binverte(in_3), .Ainverte(in_4),
    .carry_in(alu_ib_3_carry_out), .operation(in_5), .carry_out(alu_ib_4_carry_out));  // open: sign
  Alu_Ib alu_ib_5 (
    .a(in_2[4]), .b(in_1[4]), .slt(1'b0), .result(out_7[4]), .Binverte(in_3), .Ainverte(in_4),
    .carry_in(alu_ib_4_carry_out), .operation(in_5), .carry_out(alu_ib_5_carry_out));  // open: sign
  Alu_Ib alu_ib_6 (
    .a(in_2[5]), .b(in_1[5]), .slt(1'b0), .result(out_7[5]), .Binverte(in_3), .Ainverte(in_4),
    .carry_in(alu_ib_5_carry_out), .operation(in_5), .carry_out(alu_ib_6_carry_out));  // open: sign
  Alu_Ib alu_ib_7 (
    .a(in_2[6]), .b(in_1[6]), .slt(1'b0), .result(out_7[6]), .Binverte(in_3), .Ainverte(in_4),
    .carry_in(alu_ib_6_carry_out), .operation(in_5), .carry_out(alu_ib_7_carry_out));  // open: sign
  Alu_Ib alu_ib_8 (
    .a(in_2[7]), .b(in_1[7]), .slt(1'b0), .result(out_7[7]), .Binverte(in_3), .Ainverte(in_4),
    .carry_in(alu_ib_7_carry_out), .operation(in_5), .carry_out(alu_ib_8_carry_out));  // open: sign
  Alu_Ib alu_ib_9 (
    .a(in_2[8]), .b(in_1[8]), .slt(1'b0), .result(out_7[8]), .Binverte(in_3), .Ainverte(in_4),
    .carry_in(alu_ib_8_carry_out), .operation(in_5), .carry_out(alu_ib_9_carry_out));  // open: sign
  Alu_Ib alu_ib_10 (
    .a(in_2[9]), .b(in_1[9]), .slt(1'b0), .result(out_7[9]), .Binverte(in_3), .Ainverte(in_4),
    .carry_in(alu_ib_9_carry_out), .operation(in_5), .carry_out(alu_ib_10_carry_out));  // open: sign
  Alu_Ib alu_ib_11 (
    .a(in_2[10]), .b(in_1[10]), .slt(1'b0), .result(out_7[10]), .Binverte(in_3), .Ainverte(in_4),
    .carry_in(alu_ib_10_carry_out), .operation(in_5), .carry_out(alu_ib_11_carry_out));  // open: sign
  Alu_Ib alu_ib_12 (
    .a(in_2[11]), .b(in_1[11]), .slt(1'b0), .result(out_7[11]), .Binverte(in_3), .Ainverte(in_4),
    .carry_in(alu_ib_11_carry_out), .operation(in_5), .carry_out(alu_ib_12_carry_out));  // open: sign
  Alu_Ib alu_ib_13 (
    .a(in_2[12]), .b(in_1[12]), .slt(1'b0), .result(out_7[12]), .Binverte(in_3), .Ainverte(in_4),
    .carry_in(alu_ib_12_carry_out), .operation(in_5), .carry_out(alu_ib_13_carry_out));  // open: sign
  Alu_Ib alu_ib_14 (
    .a(in_2[13]), .b(in_1[13]), .slt(1'b0), .result(out_7[13]), .Binverte(in_3), .Ainverte(in_4),
    .carry_in(alu_ib_13_carry_out), .operation(in_5), .carry_out(alu_ib_14_carry_out));  // open: sign
  Alu_Ib alu_ib_15 (
    .a(in_2[14]), .b(in_1[14]), .slt(1'b0), .result(out_7[14]), .Binverte(in_3), .Ainverte(in_4),
    .carry_in(alu_ib_14_carry_out), .operation(in_5), .carry_out(alu_ib_15_carry_out));  // open: sign
  Alu_Ib alu_ib_16 (
    .a(in_2[15]), .b(in_1[15]), .slt(1'b0), .result(out_7[15]), .Binverte(in_3), .Ainverte(in_4),
    .carry_in(alu_ib_15_carry_out), .operation(in_5), .carry_out(alu_ib_16_carry_out));  // open: sign
  Alu_Ib alu_ib_17 (
    .a(in_2[16]), .b(in_1[16]), .slt(1'b0), .result(out_7[16]), .Binverte(in_3), .Ainverte(in_4),
    .carry_in(alu_ib_16_carry_out), .operation(in_5), .carry_out(alu_ib_17_carry_out));  // open: sign
  Alu_Ib alu_ib_18 (
    .a(in_2[17]), .b(in_1[17]), .slt(1'b0), .result(out_7[17]), .Binverte(in_3), .Ainverte(in_4),
    .carry_in(alu_ib_17_carry_out), .operation(in_5), .carry_out(alu_ib_18_carry_out));  // open: sign
  Alu_Ib alu_ib_19 (
    .a(in_2[18]), .b(in_1[18]), .slt(1'b0), .result(out_7[18]), .Binverte(in_3), .Ainverte(in_4),
    .carry_in(alu_ib_18_carry_out), .operation(in_5), .carry_out(alu_ib_19_carry_out));  // open: sign
  Alu_Ib alu_ib_20 (
    .a(in_2[19]), .b(in_1[19]), .slt(1'b0), .result(out_7[19]), .Binverte(in_3), .Ainverte(in_4),
    .carry_in(alu_ib_19_carry_out), .operation(in_5), .carry_out(alu_ib_20_carry_out));  // open: sign
  Alu_Ib alu_ib_21 (
    .a(in_2[20]), .b(in_1[20]), .slt(1'b0), .result(out_7[20]), .Binverte(in_3), .Ainverte(in_4),
    .carry_in(alu_ib_20_carry_out), .operation(in_5), .carry_out(alu_ib_21_carry_out));  // open: sign
  Alu_Ib alu_ib_22 (
    .a(in_2[21]), .b(in_1[21]), .slt(1'b0), .result(out_7[21]), .Binverte(in_3), .Ainverte(in_4),
    .carry_in(alu_ib_21_carry_out), .operation(in_5), .carry_out(alu_ib_22_carry_out));  // open: sign
  Alu_Ib alu_ib_23 (
    .a(in_2[22]), .b(in_1[22]), .slt(1'b0), .result(out_7[22]), .Binverte(in_3), .Ainverte(in_4),
    .carry_in(alu_ib_22_carry_out), .operation(in_5), .carry_out(alu_ib_23_carry_out));  // open: sign
  Alu_Ib alu_ib_24 (
    .a(in_2[23]), .b(in_1[23]), .slt(1'b0), .result(out_7[23]), .Binverte(in_3), .Ainverte(in_4),
    .carry_in(alu_ib_23_carry_out), .operation(in_5), .carry_out(alu_ib_24_carry_out));  // open: sign
  Alu_Ib alu_ib_25 (
    .a(in_2[24]), .b(in_1[24]), .slt(1'b0), .result(out_7[24]), .Binverte(in_3), .Ainverte(in_4),
    .carry_in(alu_ib_24_carry_out), .operation(in_5), .carry_out(alu_ib_25_carry_out));  // open: sign
  Alu_Ib alu_ib_26 (
    .a(in_2[25]), .b(in_1[25]), .slt(1'b0), .result(out_7[25]), .Binverte(in_3), .Ainverte(in_4),
    .carry_in(alu_ib_25_carry_out), .operation(in_5), .carry_out(alu_ib_26_carry_out));  // open: sign
  Alu_Ib alu_ib_27 (
    .a(in_2[26]), .b(in_1[26]), .slt(1'b0), .result(out_7[26]), .Binverte(in_3), .Ainverte(in_4),
    .carry_in(alu_ib_26_carry_out), .operation(in_5), .carry_out(alu_ib_27_carry_out));  // open: sign
  Alu_Ib alu_ib_28 (
    .a(in_2[27]), .b(in_1[27]), .slt(1'b0), .result(out_7[27]), .Binverte(in_3), .Ainverte(in_4),
    .carry_in(alu_ib_27_carry_out), .operation(in_5), .carry_out(alu_ib_28_carry_out));  // open: sign
  Alu_Ib alu_ib_29 (
    .a(in_2[28]), .b(in_1[28]), .slt(1'b0), .result(out_7[28]), .Binverte(in_3), .Ainverte(in_4),
    .carry_in(alu_ib_28_carry_out), .operation(in_5), .carry_out(alu_ib_29_carry_out));  // open: sign
  Alu_Ib alu_ib_30 (
    .a(in_2[29]), .b(in_1[29]), .slt(1'b0), .result(out_7[29]), .Binverte(in_3), .Ainverte(in_4),
    .carry_in(alu_ib_29_carry_out), .operation(in_5), .carry_out(alu_ib_30_carry_out));  // open: sign
  Alu_Ib alu_ib_31 (
    .a(in_2[30]), .b(in_1[30]), .slt(1'b0), .result(out_7[30]), .Binverte(in_3), .Ainverte(in_4),
    .carry_in(alu_ib_30_carry_out), .operation(in_5), .carry_out(alu_ib_31_carry_out));  // open: sign
  Alu_Ib alu_ib_32 (
    .a(in_2[31]), .b(in_1[31]), .slt(1'b0), .result(out_7[31]), .Binverte(in_3), .Ainverte(in_4),
    .carry_in(alu_ib_31_carry_out), .operation(in_5), .sign(alu_ib_32_sign));  // open: carry_out
  nor nor_1 (zero, out_7[0], out_7[1], out_7[2], out_7[3], out_7[4], out_7[5], out_7[6], out_7[7], out_7[8], out_7[9], out_7[10], out_7[11], out_7[12], out_7[13], out_7[14], out_7[15], out_7[16], out_7[17], out_7[18], out_7[19], out_7[20], out_7[21], out_7[22], out_7[23], out_7[24], out_7[25], out_7[26], out_7[27], out_7[28], out_7[29], out_7[30], out_7[31]);

  // Notes on the sheet:
  //   B
  //   A
endmodule
