// Logisim project New_Control_unit.circ as structural Verilog: 1 circuit, main circuit main
module main (
  input  OP0,
  input  OP1,
  input  OP2,
  input  OP3,
  input  OP4,
  input  OP5,
  output RegDst,
  output ALUSrc,
  output MemtoReg,
  output RegWrite,
  output MemRead,
  output MemWrite,
  output ExtOp,
  output Branch,
  output Jump,
  output ALUOp0,
  output ALUOp1,
  output ALUOp2
);

  wire Addi_out, Andi_out, bne_out, jal_out, lui_out, Xori_out;

  and jal (jal_out, ~OP5, ~OP4, ~OP3, ~OP2, OP1, OP0);  // AND_Gate
  and Xori (Xori_out, ~OP5, ~OP4, OP3, OP2, OP1, ~OP0);  // AND_Gate
  and bne (bne_out, ~OP5, ~OP4, ~OP3, OP2, ~OP1, OP0);  // AND_Gate
  and Addi (Addi_out, ~OP5, ~OP4, OP3, ~OP2, ~OP1, ~OP0);  // AND_Gate
  and Andi (Andi_out, ~OP5, ~OP4, OP3, OP2, ~OP1, ~OP0);  // AND_Gate
  and lui (lui_out, ~OP5, ~OP4, OP3, OP2, OP1, OP0);  // AND_Gate
  and ori (ALUOp1, ~OP5, ~OP4, OP3, OP2, ~OP1, OP0);  // AND_Gate
  and j (Jump, ~OP5, ~OP4, ~OP3, ~OP2, OP1, ~OP0);  // AND_Gate
  and beq (ALUOp0, ~OP5, ~OP4, ~OP3, OP2, ~OP1, ~OP0);  // AND_Gate
  and sw (MemWrite, OP5, ~OP4, OP3, ~OP2, OP1, OP0);  // AND_Gate
  and lw (MemRead, OP5, ~OP4, ~OP3, ~OP2, OP1, OP0);  // AND_Gate
  and r_type (ALUOp2, ~OP5, ~OP4, ~OP3, ~OP2, ~OP1, ~OP0);  // AND_Gate
  or or_1 (ALUSrc, MemRead, MemWrite, ALUOp1);
  or or_2 (RegWrite, ALUOp2, MemRead, ALUOp1);
  or or_3 (ExtOp, MemRead, MemWrite, ALUOp0);

  assign Branch = ALUOp0;
  assign MemtoReg = MemRead;
  assign RegDst = ALUOp2;
endmodule
