// Logisim project control.circ as structural Verilog: 1 circuit, main circuit main
module main (
  input  op_0,
  input  op_1,
  input  op_2,
  input  op_3,
  input  op_4,
  input  op_5,
  output Reg_Dst,
  output Alu_src,
  output mem_to_reg,
  output reg_write,
  output mem_read,
  output mem_write,
  output ext_op,
  output branch,
  output jump,
  output Alu_op0,
  output Alu_op1,
  output Alu_op2
);

  wire Addi_out, Andi_out, Bne_out, Jal_out, lui_out, ori_out, Xori_out;

  and lui (lui_out, ~op_5, ~op_4, op_3, op_2, op_1, op_0);  // AND_Gate
  and ori (ori_out, ~op_5, ~op_4, op_3, op_2, ~op_1, op_0);  // AND_Gate
  and Andi (Andi_out, ~op_5, ~op_4, op_3, op_2, ~op_1, ~op_0);  // AND_Gate
  and Addi (Addi_out, ~op_5, ~op_4, op_3, ~op_2, ~op_1, ~op_0);  // AND_Gate
  and Xori (Xori_out, ~op_5, ~op_4, op_3, op_2, op_1, ~op_0);  // AND_Gate
  and Bne (Bne_out, ~op_5, ~op_4, ~op_3, op_2, ~op_1, op_0);  // AND_Gate
  and Jal (Jal_out, ~op_5, ~op_4, ~op_3, ~op_2, op_1, op_0);  // AND_Gate
endmodule
